// Logisim project multiplexor.circ as structural Verilog: 1 circuit, main circuit main
module main (
  input  d0,
  input  sel,
  input  d1,
  output out_4
);

  wire and_1_out, and_2_out, not_1_out;

  not not_1 (not_1_out, sel);
  and and_1 (and_1_out, d0, not_1_out);
  and and_2 (and_2_out, sel, d1);
  or or_1 (out_4, and_1_out, and_2_out);
endmodule
